# Fritzing sketch irrigation (saved by Fritzing 0.9.2b)
perfboards: 1
stripboards: 1

parts:
  R1 = Resistor [tolerance=±5% resistance=10k package=THT]
  Q1 = NPN-Transistor [package="TO92 [THT]"]
  J1 = Basic Servo
  R2 = Resistor [tolerance=±5% resistance=68k package=THT]
  R3 = Resistor [tolerance=±5% resistance=56k package=THT]
  R4 = Resistor [tolerance=±5% resistance=56k package=THT]
  R5 = Resistor [tolerance=±5% resistance=68k package=THT]
  ZS-042_RTC1 = ZS-042 RTC Module
  F1 = Resettable Fuse PTC [package=ptc]
  J18 = female pin header, 2 pins [form="♀ (female)"]
  J19 = female pin header, 5 pins [form="♀ (female)"]
  J16 = female pin header, 1 pin [form="♀ (female)"]
  J15 = female pin header, 1 pin [form="♀ (female)"]
  J14 = female pin header, 1 pin [form="♀ (female)"]
  J13 = female pin header, 1 pin [form="♀ (female)"]
  J12 = female pin header, 1 pin [form="♀ (female)"]
  J11 = female pin header, 1 pin [form="♀ (female)"]
  J10 = female pin header, 1 pin [form="♀ (female)"]
  J9 = female pin header, 1 pin [form="♀ (female)"]
  J8 = female pin header, 1 pin [form="♀ (female)"]
  J7 = female pin header, 1 pin [form="♀ (female)"]
  J6 = female pin header, 1 pin [form="♀ (female)"]
  J5 = female pin header, 1 pin [form="♀ (female)"]
  J4 = female pin header, 1 pin [form="♀ (female)"]
  J17 = female pin header, 1 pin [form="♀ (female)"]
  IC1 = Arduino Pro Mini v13
  R7 = Resistor [tolerance=±5% resistance=68k package=THT]
  R9 = Resistor [tolerance=±5% resistance=56k package=THT]

nets:
  N1: R1.Pin_0, IC1.D2
  N2: R1.Pin_1, Q1.B
  GND: Q1.E, J1.gnd, R3.Pin_0, R4.Pin_0, ZS-042_RTC1.GND, J19.pin1, J14.pin1, J10.pin1, J4.pin1, IC1.GND, R9.Pin_1
  PS_ON: Q1.C, J13.pin1
  N3: J1.vcc, J15.pin1, J11.pin1, IC1.A3
  N4: J1.pulse, J12.pin1, IC1.D3_PWM
  N5: R2.Pin_0, J6.pin1, J5.pin1
  N6: R2.Pin_1, R3.Pin_1, IC1.D8
  N7: R4.Pin_1, R5.Pin_1, IC1.D6_PWM
  12V: R5.Pin_0, F1.1, J16.pin1, J8.pin1, J7.pin1, R7.Pin_0
  5V: ZS-042_RTC1.VCC, J19.pin2, J17.pin1, IC1.RAW
  N8: ZS-042_RTC1.SDA, J18.pin1, J19.pin3
  N9: ZS-042_RTC1.SCL, J18.pin2, J19.pin4
  N10: F1.2, J9.pin1
  N11: J19.pin5, IC1.D5_PWM
  N12: IC1.A1, R7.Pin_1, R9.Pin_0

notes:
  Butt Level Sensor
  Tank Level Sensor
  Pump
